# Fritzing sketch Proje (saved by Fritzing 0.9.3b)

parts:
  Parça1 = Arduino Uno (Rev3)
  SD_card_module1 = SD Card Module
  Parça2 = RFID-RC522-v2
  SP1 = SPEAKER [package=pcb_mount_speaker]

nets:
  N1: Parça1.D8, Parça2.SDA
  N2: Parça1.D9_PWM, SP1.-
  N3: Parça1.D10_PWM/SS, Parça2.RST
  N4: Parça1.D11_PWM/MOSI, SD_card_module1.MOSI, Parça2.MOSI
  N5: Parça1.D12/MISO, SD_card_module1.MISO, Parça2.MISO
  N6: Parça1.D13/SCK, SD_card_module1.SCK, Parça2.SCK
  GND: Parça1.GND, SD_card_module1.GND, Parça2.GND, SP1.+
  N7: Parça1.D4, SD_card_module1.CS
  3V3: Parça1.3V3, Parça2.3.3V
  N8: Parça1.5V, SD_card_module1.+5

custom parts:
  SD Card Module: SD Card Module Slot Socket Reader For Arduino ARM MCU
  RFID-RC522-v2: A simple China made RFID-RC522 Reader; do check the pin labels, as this is a MFRC522 based clone.
